// Logisim project SAP04.circ as structural Verilog: 10 circuits, main circuit SAP
module SAP (
  input  CLR,
  output [3:0] High,
  output [3:0] Low,
  output out_4,
  output out_5,
  output out_6,
  output out_7,
  output out_8,
  output out_9,
  output out_10,
  output out_11
);

  wire clock_1_out, Control_Sequence_cp, Control_Sequence_ea, Control_Sequence_ep, Control_Sequence_eu,
       Control_Sequence_hlt, Control_Sequence_nce, Control_Sequence_nel, Control_Sequence_nla,
       Control_Sequence_nlb, Control_Sequence_nll, Control_Sequence_nlm, Control_Sequence_nlo,
       Control_Sequence_su, controlled_buffer_1_out, controlled_buffer_7_out, not_1_out, not_2_out,
       not_3_out, not_4_out, not_5_out, not_6_out, not_7_out, not_8_out, not_9_out;
  wire [3:0] Counter_q, IR_lsbout, IR_msbout, MAR_lsbout, RegisterA_lsbout, RegisterA_msbout;
  wire [7:0] adder_1_out, controlled_inverter_1_out, RegisterB_lsbout;

  Counter #(.width(4), .max('hf), .trigger("falling")) Counter (
    .Q(Counter_q), .clk(controlled_buffer_1_out), .clr(CLR));  // open: load, D, count, carry
  assign controlled_buffer_1_out = Control_Sequence_cp ? controlled_buffer_7_out : 1'bz;  // Controlled_Buffer controlled_buffer_1
  not not_1 (not_1_out, Control_Sequence_nlm);
  not not_2 (not_2_out, Control_Sequence_nce);
  register IR (
    .LSBIN(Low), .MSBIN(High), .Load(not_3_out), .Clk(controlled_buffer_7_out), .Clr(CLR),
    .MSBOUT(IR_msbout), .LSBOUT(IR_lsbout));
  not not_3 (not_3_out, Control_Sequence_nll);
  controlSequencer Control_Sequence (
    .CLK(controlled_buffer_7_out), .CLR(CLR), .Ep(Control_Sequence_ep), .Cp(Control_Sequence_cp),
    .l7(IR_msbout[3]), .l6(IR_msbout[2]), .l5(IR_msbout[1]), .l4(IR_msbout[0]), .HLT(Control_Sequence_hlt),
    .nLm(Control_Sequence_nlm), .nCE(Control_Sequence_nce), .nEl(Control_Sequence_nel),
    .nLa(Control_Sequence_nla), .Ea(Control_Sequence_ea), .Su(Control_Sequence_su), .Eu(Control_Sequence_eu),
    .nLb(Control_Sequence_nlb), .nLo(Control_Sequence_nlo), .nLl(Control_Sequence_nll));
  assign Low = Control_Sequence_ep ? Counter_q : 4'bz;  // Controlled_Buffer controlled_buffer_2
  register MAR (
    .LSBIN(Low), .Load(not_1_out), .Clk(controlled_buffer_7_out), .Clr(CLR), .LSBOUT(MAR_lsbout));  // open: MSBIN, MSBOUT
  RAM #(.addrWidth(4)) ram_1 (.addr(MAR_lsbout), .data({High, Low}), .ld(not_2_out));  // open: sel, clk, clr
  assign Low = not_4_out ? IR_lsbout : 4'bz;  // Controlled_Buffer controlled_buffer_3
  not not_4 (not_4_out, Control_Sequence_nel);
  assign {High, Low} = Control_Sequence_ea ? {RegisterA_msbout, RegisterA_lsbout} : 8'bz;  // Controlled_Buffer controlled_buffer_4
  assign {High, Low} = Control_Sequence_eu ? adder_1_out : 8'bz;  // Controlled_Buffer controlled_buffer_5
  register RegisterA (
    .LSBIN(Low), .MSBIN(High), .Load(not_5_out), .Clk(controlled_buffer_7_out), .Clr(CLR),
    .MSBOUT(RegisterA_msbout), .LSBOUT(RegisterA_lsbout));
  Adder adder_1 (
    .a({RegisterA_msbout, RegisterA_lsbout}), .b(controlled_inverter_1_out), .out(adder_1_out),
    .cin(Control_Sequence_su));  // open: cout
  not not_5 (not_5_out, Control_Sequence_nla);
  assign controlled_inverter_1_out = Control_Sequence_su ? ~RegisterB_lsbout : 8'bz;  // Controlled_Inverter controlled_inverter_1
  not not_6 (not_6_out, Control_Sequence_nlb);
  register \output  (
    .LSBIN(Low), .MSBIN(High), .Load(not_7_out), .Clk(controlled_buffer_7_out), .Clr(CLR),
    .MSBOUT({out_11, out_10, out_9, out_8}), .LSBOUT({out_7, out_6, out_5, out_4}));
  not not_7 (not_7_out, Control_Sequence_nlo);
  assign controlled_inverter_1_out = not_8_out ? RegisterB_lsbout : 8'bz;  // Controlled_Buffer controlled_buffer_6
  not not_8 (not_8_out, Control_Sequence_su);
  Clock clock_1 (.out(clock_1_out));
  not not_9 (not_9_out, Control_Sequence_hlt);
  assign controlled_buffer_7_out = not_9_out ? clock_1_out : 1'bz;  // Controlled_Buffer controlled_buffer_7
  register RegisterB (
    .LSBIN(Low), .MSBIN(High), .Load(not_6_out), .Clk(controlled_buffer_7_out), .Clr(CLR),
    .MSBOUT(RegisterB_lsbout[7:4]), .LSBOUT(RegisterB_lsbout[3:0]));
  Hex_Digit_Display hex_digit_display_1 (.value({out_11, out_10, out_9, out_8}));  // open: dp
  Hex_Digit_Display hex_digit_display_2 (.value({out_7, out_6, out_5, out_4}));  // open: dp

  // Notes on the sheet:
  //   ADD/SUB
endmodule

module registerUnit (
  input  Xi,
  input  Load,
  input  Clk,
  input  Clr,
  input  Enable,
  output Yi
);

  wire and_1_out, and_2_out, d_ff_1_q, not_1_out, or_1_out;

  not not_1 (not_1_out, Load);
  and and_1 (and_1_out, Load, Xi);
  and and_2 (and_2_out, not_1_out, d_ff_1_q);
  or or_1 (or_1_out, and_1_out, and_2_out);
  D_Flip_Flop d_ff_1 (.clk(Clk), .D(or_1_out), .Q(d_ff_1_q), .reset(Clr));  // open: Qn, preset, en
  assign Yi = Enable ? d_ff_1_q : 1'bz;  // Controlled_Buffer controlled_buffer_1
endmodule

module register (
  input  [3:0] LSBIN,
  input  [3:0] MSBIN,
  input  Load,
  input  Clk,
  input  Clr,
  output [3:0] MSBOUT,
  output [3:0] LSBOUT
);

  registerUnit R7 (.Xi(MSBIN[3]), .Load(Load), .Clk(Clk), .Clr(Clr), .Enable(1'b1), .Yi(MSBOUT[3]));
  registerUnit R6 (.Xi(MSBIN[2]), .Load(Load), .Clk(Clk), .Clr(Clr), .Enable(1'b1), .Yi(MSBOUT[2]));
  registerUnit R5 (.Xi(MSBIN[1]), .Load(Load), .Clk(Clk), .Clr(Clr), .Enable(1'b1), .Yi(MSBOUT[1]));
  registerUnit R4 (.Xi(MSBIN[0]), .Load(Load), .Clk(Clk), .Clr(Clr), .Enable(1'b1), .Yi(MSBOUT[0]));
  registerUnit R3 (.Xi(LSBIN[3]), .Load(Load), .Clk(Clk), .Clr(Clr), .Enable(1'b1), .Yi(LSBOUT[3]));
  registerUnit R2 (.Xi(LSBIN[2]), .Load(Load), .Clk(Clk), .Clr(Clr), .Enable(1'b1), .Yi(LSBOUT[2]));
  registerUnit R1 (.Xi(LSBIN[1]), .Load(Load), .Clk(Clk), .Clr(Clr), .Enable(1'b1), .Yi(LSBOUT[1]));
  registerUnit R0 (.Xi(LSBIN[0]), .Load(Load), .Clk(Clk), .Clr(Clr), .Enable(1'b1), .Yi(LSBOUT[0]));
endmodule

module controlSequencer (
  input  CLK,
  input  CLR,
  input  l7,
  input  l5,
  input  l6,
  input  l4,
  output Ep,
  output Cp,
  output HLT,
  output nLm,
  output nCE,
  output nEl,
  output nLa,
  output Ea,
  output Su,
  output Eu,
  output nLb,
  output nLo,
  output nLl
);

  wire c39_1_out_7, c39_1_out_8, c39_1_out_9, c39_1_out_10, c40_1_out_7, c40_1_out_8, c40_1_out_9,
       c40_1_out_10, c41_1_out_8, c41_1_out_9, c41_1_out_10, c41_1_out_11, c41_2_out_10, c41_2_out_11,
       c43_1_out_6, c43_1_out_7, c43_1_out_8, Instruction_Decoder_add, Instruction_Decoder_lda,
       Instruction_Decoder_out, Instruction_Decoder_sub, nor_1_out, not_1_out, shift_register_1_q2,
       shift_register_1_q3, shift_register_1_q4, shift_register_1_q5;

  instructionDecoder Instruction_Decoder (
    .l7(l7), .l6(l6), .l5(l5), .l4(l4), .LDA(Instruction_Decoder_lda), .ADD(Instruction_Decoder_add),
    .SUB(Instruction_Decoder_sub), .OUT(Instruction_Decoder_out), .HLT(HLT));
  C39 c39_1 (
    ._1(Instruction_Decoder_lda), ._4(Instruction_Decoder_add), ._9(Instruction_Decoder_sub),
    ._10(shift_register_1_q3), ._12(Instruction_Decoder_lda), ._13(shift_register_1_q4), .out_7(c39_1_out_7),
    .out_8(c39_1_out_8), .out_9(c39_1_out_9), .out_10(c39_1_out_10));
  not not_1 (not_1_out, CLK);
  C40 c40_1 (
    ._1(Instruction_Decoder_add), ._4(Instruction_Decoder_sub), ._5(shift_register_1_q4),
    ._9(Instruction_Decoder_lda), ._12(Instruction_Decoder_add), ._13(shift_register_1_q3),
    .out_7(c40_1_out_7), .out_8(c40_1_out_8), .out_9(c40_1_out_9), .out_10(c40_1_out_10));
  \module  module_1 (
    .in_1(Ep), .in_2(c39_1_out_7), .in_3(c39_1_out_8), .in_4(c39_1_out_9), .in_5(shift_register_1_q2),
    .in_6(c39_1_out_10), .in_7(c40_1_out_7), .in_8(c40_1_out_8), .in_9(c40_1_out_9), .in_10(c40_1_out_10),
    .in_11(c41_1_out_8), .in_12(c41_1_out_9), .in_13(c41_1_out_10), .in_14(c41_1_out_11),
    .in_15(c41_2_out_10), .in_16(c41_2_out_11), .in_17(c43_1_out_6), .in_18(c43_1_out_7), .out_19(nLm),
    .out_20(nCE), .out_21(nEl), .out_22(nLa), .out_23(Eu), .out_24(nLb));
  Shift_Register #(.length(6)) shift_register_1 (
    .in(nor_1_out), .clk(not_1_out), .clr(CLR), .q0(Ep), .q1(Cp), .q2(shift_register_1_q2),
    .q3(shift_register_1_q3), .q4(shift_register_1_q4), .q5(shift_register_1_q5));  // open: shift, out, load, d0, d1, d2, d3, d4, d5
  C41 c41_1 (
    ._1(Instruction_Decoder_sub), ._2(shift_register_1_q3), ._4(Instruction_Decoder_lda),
    ._5(shift_register_1_q4), ._9(Instruction_Decoder_add), ._12(Instruction_Decoder_sub),
    ._13(shift_register_1_q5), .out_8(c41_1_out_8), .out_9(c41_1_out_9), .out_10(c41_1_out_10),
    .out_11(c41_1_out_11));
  C41 c41_2 (
    ._1(Instruction_Decoder_out), ._2(shift_register_1_q3), ._4(Instruction_Decoder_sub),
    ._5(shift_register_1_q5), ._9(Instruction_Decoder_add), ._12(Instruction_Decoder_sub),
    ._13(shift_register_1_q5), .out_8(Ea), .out_9(Su), .out_10(c41_2_out_10), .out_11(c41_2_out_11));
  C43 c43_1 (
    ._1(Instruction_Decoder_add), ._4(Instruction_Decoder_sub), ._5(shift_register_1_q4),
    ._9(Instruction_Decoder_out), ._10(shift_register_1_q3), .out_6(c43_1_out_6), .out_7(c43_1_out_7),
    .out_8(c43_1_out_8));
  nor nor_1 (nor_1_out, Ep, Cp, shift_register_1_q2, shift_register_1_q3, shift_register_1_q4);
  not not_2 (nLo, c43_1_out_8);
  not not_3 (nLl, shift_register_1_q2);
endmodule

module instructionDecoder (
  input  l7,
  input  l6,
  input  l5,
  input  l4,
  output LDA,
  output ADD,
  output SUB,
  output OUT,
  output HLT
);

  wire and_1_out, and_2_out, and_3_out, and_4_out, and_5_out, not_1_out, not_2_out, not_3_out, not_4_out;

  not not_1 (not_1_out, l7);
  not not_2 (not_2_out, l6);
  not not_3 (not_3_out, l5);
  not not_4 (not_4_out, l4);
  and and_1 (and_1_out, not_1_out, not_2_out, not_3_out, not_4_out);
  and and_2 (and_2_out, not_1_out, not_2_out, not_3_out, l4);
  and and_3 (and_3_out, not_1_out, not_2_out, l5, not_4_out);
  and and_4 (and_4_out, l7, l6, l5, not_4_out);
  and and_5 (and_5_out, l7, l6, l5, l4);
  buf buffer_1 (LDA, and_1_out);
  buf buffer_2 (ADD, and_2_out);
  buf buffer_3 (SUB, and_3_out);
  buf buffer_4 (OUT, and_4_out);
  buf buffer_5 (HLT, and_5_out);
endmodule

module C39 (
  input  _1,
  input  _4,
  input  _9,
  input  _10,
  input  _13,
  input  _12,
  output out_7,
  output out_8,
  output out_9,
  output out_10
);

  and and_1 (out_7, _1, _10);
  and and_2 (out_8, _4, _10);
  and and_3 (out_9, _9, _10);
  and and_4 (out_10, _12, _13);
endmodule

module C40 (
  input  _1,
  input  _4,
  input  _5,
  input  _9,
  input  _12,
  input  _13,
  output out_7,
  output out_8,
  output out_9,
  output out_10
);

  and and_1 (out_7, _1, _5);
  and and_2 (out_8, _4, _5);
  and and_3 (out_10, _12, _13);
  and and_4 (out_9, _9, _13);
endmodule

module C41 (
  input  _4,
  input  _5,
  input  _12,
  input  _13,
  input  _1,
  input  _2,
  input  _9,
  output out_8,
  output out_9,
  output out_10,
  output out_11
);

  and and_1 (out_8, _1, _2);
  and and_2 (out_9, _4, _5);
  and and_3 (out_10, _9, _13);
  and and_4 (out_11, _12, _13);
endmodule

module C43 (
  input  _1,
  input  _4,
  input  _5,
  input  _9,
  input  _10,
  output out_6,
  output out_7,
  output out_8
);

  and and_1 (out_6, _1, _5);
  and and_2 (out_7, _4, _5);
  and and_3 (out_8, _9, _10);
endmodule

module \module  (
  input  in_1,
  input  in_2,
  input  in_3,
  input  in_4,
  input  in_5,
  input  in_6,
  input  in_7,
  input  in_8,
  input  in_9,
  input  in_10,
  input  in_11,
  input  in_12,
  input  in_13,
  input  in_14,
  input  in_15,
  input  in_16,
  input  in_17,
  input  in_18,
  output out_19,
  output out_20,
  output out_21,
  output out_22,
  output out_23,
  output out_24
);

  nor nor_1 (out_19, in_1, in_2, in_3, in_4);
  nor nor_2 (out_20, in_5, in_6, in_7, in_8);
  nor nor_3 (out_21, in_9, in_10, in_11);
  nor nor_4 (out_22, in_12, in_13, in_14);
  or or_1 (out_23, in_15, in_16);
  nor nor_5 (out_24, in_17, in_18);
endmodule
