// Logisim project sap1.circ as structural Verilog: 18 circuits, main circuit sap1
module main (
  input  CLR,
  output [3:0] High,
  output [3:0] Low,
  output out_4,
  output out_5,
  output out_6,
  output out_7,
  output out_8,
  output out_9,
  output out_10,
  output out_11
);

  wire clock_1_out, comparator_1_eq, comparator_1_gt, comparator_1_lt, controlled_buffer_1_out,
       controlled_buffer_10_out, controlmatrix_1_cp, controlmatrix_1_ea, controlmatrix_1_ec,
       controlmatrix_1_ed, controlmatrix_1_ep, controlmatrix_1_eu, controlmatrix_1_ex, controlmatrix_1_nce,
       controlmatrix_1_nei, controlmatrix_1_nhlt, controlmatrix_1_nl0, controlmatrix_1_nla,
       controlmatrix_1_nlb, controlmatrix_1_nli, controlmatrix_1_nlm, controlmatrix_1_su, not_1_out,
       not_2_out, not_3_out, not_4_out, not_5_out, not_6_out, not_7_out, not_8_out, not_9_out;
  wire [2:0] test_1_less_2;
  wire [3:0] Counter_q, IR_lsbout, IR_msbout, MAR_lsbout;
  wire [7:0] adder_1_out, controlled_buffer_9_out, divider_1_out, multiplier_1_out, RegisterA_lsbout,
       RegisterB_lsbout;

  Counter #(.width(4), .max('hf), .trigger("falling")) Counter (
    .Q(Counter_q), .clk(controlled_buffer_1_out), .clr(CLR));  // open: load, D, count, carry
  assign controlled_buffer_1_out = controlmatrix_1_cp ? controlled_buffer_10_out : 1'bz;  // Controlled_Buffer controlled_buffer_1
  not not_1 (not_1_out, controlmatrix_1_nlm);
  not not_2 (not_2_out, controlmatrix_1_nce);
  register IR (
    .LSBIN(Low), .MSBIN(High), .Load(not_3_out), .Clk(controlled_buffer_10_out), .Clr(CLR),
    .MSBOUT(IR_msbout), .LSBOUT(IR_lsbout));
  not not_3 (not_3_out, controlmatrix_1_nli);
  assign Low = controlmatrix_1_ep ? Counter_q : 4'bz;  // Controlled_Buffer controlled_buffer_2
  register MAR (
    .LSBIN(Low), .Load(not_1_out), .Clk(controlled_buffer_10_out), .Clr(CLR), .LSBOUT(MAR_lsbout));  // open: MSBIN, MSBOUT
  RAM #(.addrWidth(4)) ram_1 (.addr(MAR_lsbout), .data({High, Low}), .ld(not_2_out));  // open: sel, clk, clr
  not not_4 (not_4_out, controlmatrix_1_nei);
  assign Low = not_4_out ? IR_lsbout : 4'bz;  // Controlled_Buffer controlled_buffer_3
  ControlMatrix controlmatrix_1 (
    .nHLT(controlmatrix_1_nhlt), .I7(IR_msbout[3]), .I6(IR_msbout[2]), .I5(IR_msbout[1]), .I4(IR_msbout[0]),
    .CLR(CLR), .nCLK(controlled_buffer_10_out), .Cp(controlmatrix_1_cp), .Ep(controlmatrix_1_ep),
    .nLm(controlmatrix_1_nlm), .nCE(controlmatrix_1_nce), .nLi(controlmatrix_1_nli),
    .nEi(controlmatrix_1_nei), .nLA(controlmatrix_1_nla), .nL0(controlmatrix_1_nl0), .Su(controlmatrix_1_su),
    .Eu(controlmatrix_1_eu), .EA(controlmatrix_1_ea), .nLB(controlmatrix_1_nlb), .Ex(controlmatrix_1_ex),
    .ED(controlmatrix_1_ed), .Ec(controlmatrix_1_ec));
  assign {High, Low} = controlmatrix_1_ed ? divider_1_out : 8'bz;  // Controlled_Buffer controlled_buffer_4
  assign {High, Low} = controlmatrix_1_ex ? multiplier_1_out : 8'bz;  // Controlled_Buffer controlled_buffer_5
  assign {High, Low} = controlmatrix_1_ea ? RegisterA_lsbout : 8'bz;  // Controlled_Buffer controlled_buffer_6
  assign {High, Low} = controlmatrix_1_eu ? adder_1_out : 8'bz;  // Controlled_Buffer controlled_buffer_7
  not not_5 (not_5_out, controlmatrix_1_nla);
  assign Low = controlmatrix_1_ec ? {1'b0, test_1_less_2} : 4'bz;  // Controlled_Buffer controlled_buffer_8
  register RegisterA (
    .LSBIN(Low), .MSBIN(High), .Load(not_5_out), .Clk(controlled_buffer_10_out), .Clr(CLR),
    .MSBOUT(RegisterA_lsbout[7:4]), .LSBOUT(RegisterA_lsbout[3:0]));
  Adder adder_1 (
    .a(RegisterA_lsbout), .b(controlled_buffer_9_out), .out(adder_1_out), .cin(controlmatrix_1_su));  // open: cout
  assign controlled_buffer_9_out = not_8_out ? RegisterB_lsbout : 8'bz;  // Controlled_Buffer controlled_buffer_9
  assign controlled_buffer_9_out = controlmatrix_1_su ? ~RegisterB_lsbout : 8'bz;  // Controlled_Inverter controlled_inverter_1
  not not_6 (not_6_out, controlmatrix_1_nlb);
  register \output  (
    .LSBIN(Low), .MSBIN(High), .Load(not_7_out), .Clk(controlled_buffer_10_out), .Clr(CLR),
    .MSBOUT({out_11, out_10, out_9, out_8}), .LSBOUT({out_7, out_6, out_5, out_4}));
  not not_7 (not_7_out, controlmatrix_1_nl0);
  not not_8 (not_8_out, controlmatrix_1_su);
  Clock clock_1 (.out(clock_1_out));
  not not_9 (not_9_out, controlmatrix_1_nhlt);
  assign controlled_buffer_10_out = not_9_out ? clock_1_out : 1'bz;  // Controlled_Buffer controlled_buffer_10
  register RegisterB (
    .LSBIN(Low), .MSBIN(High), .Load(not_6_out), .Clk(controlled_buffer_10_out), .Clr(CLR),
    .MSBOUT(RegisterB_lsbout[7:4]), .LSBOUT(RegisterB_lsbout[3:0]));
  Multiplier multiplier_1 (.a(RegisterA_lsbout), .b(RegisterB_lsbout), .out(multiplier_1_out));  // open: cin, cout
  Divider divider_1 (.a(RegisterA_lsbout), .b(RegisterB_lsbout), .out(divider_1_out));  // open: upper, rem
  Hex_Digit_Display hex_digit_display_1 (.value({out_7, out_6, out_5, out_4}));  // open: dp
  Hex_Digit_Display hex_digit_display_2 (.value({out_11, out_10, out_9, out_8}));  // open: dp
  test test_1 (
    .less(comparator_1_lt), .equal(comparator_1_eq), .greater(comparator_1_gt), .less_2(test_1_less_2[0]),
    .equal_2(test_1_less_2[1]), .greater_2(test_1_less_2[2]));
  Comparator comparator_1 (
    .a(RegisterA_lsbout), .b(RegisterB_lsbout), .gt(comparator_1_gt), .eq(comparator_1_eq),
    .lt(comparator_1_lt));

  // Notes on the sheet:
  //   ADD/SUB
  //   Multipy
  //   Divide
  //   Compare
endmodule

module Instruction_Decoder (
  input  I7,
  input  I6,
  input  I5,
  input  I4,
  output LOAD,
  output ADD,
  output SUB,
  output OUT,
  output nHLT,
  output MUL,
  output DIV,
  output COMP
);

  wire c31_1_i4_2, c31_1_i5_2, c31_1_i6_2, c31_1_i7_2, c31_1_ni4, c31_1_ni5, c31_1_ni6, c31_1_ni7;

  C31 c31_1 (
    .I7(I7), .I6(I6), .I5(I5), .I4(I4), .nI7(c31_1_ni7), .I7_2(c31_1_i7_2), .nI6(c31_1_ni6),
    .I6_2(c31_1_i6_2), .nI5(c31_1_ni5), .I5_2(c31_1_i5_2), .nI4(c31_1_ni4), .I4_2(c31_1_i4_2));
  and C32 (LOAD, c31_1_ni7, c31_1_ni6, c31_1_ni5, c31_1_ni4);
  and C32_2 (ADD, c31_1_ni7, c31_1_ni6, c31_1_ni5, c31_1_i4_2);
  and C33 (SUB, c31_1_ni7, c31_1_ni6, c31_1_i5_2, c31_1_ni4);
  and C33_2 (OUT, c31_1_i7_2, c31_1_i6_2, c31_1_i5_2, c31_1_ni4);
  and and_1 (nHLT, c31_1_i7_2, c31_1_i6_2, c31_1_i5_2, c31_1_i4_2);
  and u_MUL (MUL, c31_1_ni7, c31_1_ni6, c31_1_i5_2, c31_1_i4_2);
  and u_DIV (DIV, c31_1_ni7, c31_1_i6_2, c31_1_ni5, c31_1_ni4);
  and u_COMP (COMP, c31_1_i4_2, c31_1_ni5, c31_1_i6_2, c31_1_ni7);
endmodule

module C47 (
  input  _1,
  input  _3,
  input  _5,
  input  _7,
  input  _9,
  input  _11,
  input  _13,
  output _2,
  output _4,
  output _6,
  output _8,
  output _8_2,
  output _10,
  output _12
);

  not not_1 (_2, _1);
  not not_2 (_4, _3);
  not not_3 (_6, _5);
  not not_4 (_8, _7);
  not not_5 (_8_2, _9);
  not not_6 (_10, _11);
  not not_7 (_12, _13);
endmodule

module C44 (
  input  _1,
  input  _2,
  input  _4,
  input  _5,
  input  _9,
  input  _10,
  input  _11,
  output _6
);

  or or_1 (_6, _1, _2, _4, _5, _9, _10, _11);
endmodule

module C46 (
  input  _1,
  input  _2,
  input  _4,
  input  _5,
  output _3,
  output _6
);

  or or_1 (_3, _1, _2);
  or or_2 (_6, _4, _5);
endmodule

module C45 (
  input  _1,
  input  _2,
  input  _13,
  input  _3,
  input  _4,
  input  _5,
  output _12,
  output _6
);

  or or_1 (_12, _1, _2, _13);
  or or_2 (_6, _3, _4, _5);
endmodule

// Control Matrix
module ControlMatrix (
  input  CLR,
  input  nCLK,
  input  I7,
  input  I6,
  input  I5,
  input  I4,
  output nHLT,
  output Cp,
  output Ep,
  output nLm,
  output nCE,
  output nLi,
  output nEi,
  output nLA,
  output nL0,
  output Su,
  output Eu,
  output EA,
  output nLB,
  output Ex,
  output ED,
  output Ec
);

  wire C39__3, C39__6, C39__8, C39__11, c44_1__6, c44_2__6, c48_1__8, c48_2__8, c48_3__8,
       instruction_decoder_1_add, instruction_decoder_1_comp, instruction_decoder_1_div,
       instruction_decoder_1_load, instruction_decoder_1_mul, instruction_decoder_1_out,
       instruction_decoder_1_sub, n4_and_1__3, n4_and_1__6, n4_and_1__8, n4_and_1__11, n4_and_2__3,
       n4_and_2__6, n4_and_2__8, n4_and_2__11, n4_and_3__3, n4_and_3__6, n4_and_3__8, n4_and_3__11,
       n4_and_4__3, n4_and_4__6, n4_and_4__8, n4_and_4__11, n4_and_5__3, n4_and_5__6, n4_and_5__8,
       n4_and_5__11, n4_and_6__8, n4_and_6__11, n4_and_7__3, n4_and_7__6, n4_and_7__8, n4_and_7__11,
       n4_and_8__3, nor_1_out, not_1_out, shift_register_1_q2, shift_register_1_q3, shift_register_1_q4,
       shift_register_1_q5;

  Instruction_Decoder instruction_decoder_1 (
    .I7(I7), .I6(I6), .I5(I5), .I4(I4), .LOAD(instruction_decoder_1_load), .ADD(instruction_decoder_1_add),
    .SUB(instruction_decoder_1_sub), .OUT(instruction_decoder_1_out), .nHLT(nHLT),
    .MUL(instruction_decoder_1_mul), .DIV(instruction_decoder_1_div), .COMP(instruction_decoder_1_comp));
  _4_AND C39 (
    ._1(instruction_decoder_1_load), ._2(shift_register_1_q3), ._4(instruction_decoder_1_add),
    ._5(shift_register_1_q3), ._9(instruction_decoder_1_sub), ._10(shift_register_1_q3),
    ._12(instruction_decoder_1_mul), ._13(shift_register_1_q3), ._3(C39__3), ._6(C39__6), ._8(C39__8),
    ._11(C39__11));
  _4_AND u_4_and_1 (
    ._1(instruction_decoder_1_div), ._2(shift_register_1_q3), ._4(instruction_decoder_1_comp),
    ._5(shift_register_1_q3), ._9(instruction_decoder_1_load), ._10(shift_register_1_q4),
    ._12(instruction_decoder_1_add), ._13(shift_register_1_q4), ._3(n4_and_1__3), ._6(n4_and_1__6),
    ._8(n4_and_1__8), ._11(n4_and_1__11));
  C44 c44_1 (
    ._1(n4_and_1__6), ._2(n4_and_1__3), ._4(C39__11), ._5(C39__8), ._9(C39__6), ._10(C39__3), ._11(Ep),
    ._6(c44_1__6));
  not not_1 (not_1_out, nCLK);
  Shift_Register #(.length(6)) shift_register_1 (
    .in(nor_1_out), .clk(not_1_out), .clr(CLR), .q0(Ep), .q1(Cp), .q2(shift_register_1_q2),
    .q3(shift_register_1_q3), .q4(shift_register_1_q4), .q5(shift_register_1_q5));  // open: shift, out, load, d0, d1, d2, d3, d4, d5
  _4_AND u_4_and_2 (
    ._1(instruction_decoder_1_sub), ._2(shift_register_1_q4), ._4(instruction_decoder_1_mul),
    ._5(shift_register_1_q4), ._9(instruction_decoder_1_div), ._10(shift_register_1_q4),
    ._12(instruction_decoder_1_comp), ._13(shift_register_1_q4), ._3(n4_and_2__3), ._6(n4_and_2__6),
    ._8(n4_and_2__8), ._11(n4_and_2__11));
  C44 c44_2 (
    ._1(shift_register_1_q2), ._2(n4_and_2__11), ._4(n4_and_2__8), ._5(n4_and_2__6), ._9(n4_and_2__3),
    ._10(n4_and_1__11), ._11(n4_and_1__8), ._6(c44_2__6));
  nor nor_1 (nor_1_out, shift_register_1_q5, shift_register_1_q4, shift_register_1_q3, shift_register_1_q2, Cp, Ep);
  _4_AND u_4_and_3 (
    ._1(instruction_decoder_1_load), ._2(shift_register_1_q3), ._4(instruction_decoder_1_add),
    ._5(shift_register_1_q3), ._9(instruction_decoder_1_sub), ._10(shift_register_1_q3),
    ._12(instruction_decoder_1_mul), ._13(shift_register_1_q3), ._3(n4_and_3__3), ._6(n4_and_3__6),
    ._8(n4_and_3__8), ._11(n4_and_3__11));
  C47 c47_1 (
    ._3(EA), ._5(c48_2__8), ._7(c48_1__8), ._9(shift_register_1_q2), ._11(c44_2__6), ._13(c44_1__6),
    ._4(nL0), ._6(nLA), ._8(nEi), ._8_2(nLi), ._10(nCE), ._12(nLm));  // open: _1, _2
  _4_AND u_4_and_4 (
    ._1(instruction_decoder_1_div), ._2(shift_register_1_q3), ._4(instruction_decoder_1_comp),
    ._5(shift_register_1_q3), ._9(instruction_decoder_1_load), ._10(shift_register_1_q4),
    ._12(instruction_decoder_1_add), ._13(shift_register_1_q5), ._3(n4_and_4__3), ._6(n4_and_4__6),
    ._8(n4_and_4__8), ._11(n4_and_4__11));
  C48 c48_1 (
    ._10(n4_and_4__6), ._9(n4_and_4__3), ._6(n4_and_3__11), ._5(n4_and_3__8), ._2(n4_and_3__6),
    ._1(n4_and_3__3), ._8(c48_1__8));  // open: _13, _12, _11
  _4_AND u_4_and_5 (
    ._1(instruction_decoder_1_sub), ._2(shift_register_1_q5), ._4(instruction_decoder_1_mul),
    ._5(shift_register_1_q5), ._9(instruction_decoder_1_div), ._10(shift_register_1_q5),
    ._12(instruction_decoder_1_comp), ._13(shift_register_1_q5), ._3(n4_and_5__3), ._6(n4_and_5__6),
    ._8(n4_and_5__8), ._11(n4_and_5__11));
  C48 c48_2 (
    ._13(n4_and_6__11), ._12(n4_and_6__8), ._10(n4_and_5__11), ._9(n4_and_5__8), ._6(n4_and_5__6),
    ._5(n4_and_5__3), ._2(n4_and_4__11), ._1(n4_and_4__8), ._11(Eu), ._8(c48_2__8));
  _4_AND u_4_and_6 (
    ._1(instruction_decoder_1_out), ._2(shift_register_1_q3), ._4(instruction_decoder_1_sub),
    ._5(shift_register_1_q5), ._9(instruction_decoder_1_add), ._10(shift_register_1_q5),
    ._12(instruction_decoder_1_sub), ._13(shift_register_1_q5), ._3(EA), ._6(Su), ._8(n4_and_6__8),
    ._11(n4_and_6__11));
  _4_AND u_4_and_7 (
    ._1(instruction_decoder_1_add), ._2(shift_register_1_q4), ._4(instruction_decoder_1_sub),
    ._5(shift_register_1_q4), ._9(instruction_decoder_1_mul), ._10(shift_register_1_q4),
    ._12(instruction_decoder_1_div), ._13(shift_register_1_q4), ._3(n4_and_7__3), ._6(n4_and_7__6),
    ._8(n4_and_7__8), ._11(n4_and_7__11));
  _4_AND u_4_and_8 (
    ._1(instruction_decoder_1_comp), ._2(shift_register_1_q4), ._4(instruction_decoder_1_mul),
    ._5(shift_register_1_q5), ._9(instruction_decoder_1_div), ._10(shift_register_1_q5),
    ._12(instruction_decoder_1_comp), ._13(shift_register_1_q5), ._3(n4_and_8__3), ._6(Ex), ._8(ED), ._11(Ec));
  C48 c48_3 (
    ._10(n4_and_8__3), ._9(n4_and_8__3), ._6(n4_and_7__11), ._5(n4_and_7__8), ._2(n4_and_7__6),
    ._1(n4_and_7__3), ._8(c48_3__8));  // open: _13, _12, _11
  not not_2 (nLB, c48_3__8);
endmodule

module Register4bit (
  input  load,
  input  clear,
  input  clock,
  input  Enable,
  input  [3:0] in,
  output [3:0] out
);

  wire and_1_out, and_2_out, and_3_out, and_4_out, and_5_out, and_6_out, and_7_out, and_8_out, d_ff_1_q,
       d_ff_2_q, d_ff_3_q, d_ff_4_q, not_1_out, or_1_out, or_2_out, or_3_out, or_4_out;

  not not_1 (not_1_out, load);
  and and_1 (and_1_out, in[3], load);
  and and_2 (and_2_out, not_1_out, d_ff_1_q);
  or or_1 (or_1_out, and_1_out, and_2_out);
  D_Flip_Flop d_ff_1 (.clk(clock), .D(or_1_out), .Q(d_ff_1_q), .reset(clear));  // open: Qn, preset, en
  assign out[3] = Enable ? d_ff_1_q : 1'bz;  // Controlled_Buffer controlled_buffer_1
  and and_3 (and_3_out, in[2], load);
  and and_4 (and_4_out, not_1_out, d_ff_2_q);
  or or_2 (or_2_out, and_3_out, and_4_out);
  D_Flip_Flop d_ff_2 (.clk(clock), .D(or_2_out), .Q(d_ff_2_q), .reset(clear));  // open: Qn, preset, en
  assign out[2] = Enable ? d_ff_2_q : 1'bz;  // Controlled_Buffer controlled_buffer_2
  and and_5 (and_5_out, in[1], load);
  and and_6 (and_6_out, not_1_out, d_ff_3_q);
  or or_3 (or_3_out, and_5_out, and_6_out);
  D_Flip_Flop d_ff_3 (.clk(clock), .D(or_3_out), .Q(d_ff_3_q), .reset(clear));  // open: Qn, preset, en
  assign out[1] = Enable ? d_ff_3_q : 1'bz;  // Controlled_Buffer controlled_buffer_3
  and and_7 (and_7_out, in[0], load);
  and and_8 (and_8_out, not_1_out, d_ff_4_q);
  or or_4 (or_4_out, and_7_out, and_8_out);
  D_Flip_Flop d_ff_4 (.clk(clock), .D(or_4_out), .Q(d_ff_4_q), .reset(clear));  // open: Qn, preset, en
  assign out[0] = Enable ? d_ff_4_q : 1'bz;  // Controlled_Buffer controlled_buffer_4
endmodule

module Register8bit (
  input  [7:0] in,
  input  Load,
  input  clear,
  input  clock,
  input  Enable,
  output [7:0] out
);

  Register4bit register4bit_1 (
    .load(Load), .clear(clear), .clock(clock), .Enable(Enable), .out(out[7:4]), .in(in[7:4]));
  Register4bit register4bit_2 (
    .load(Load), .clear(clear), .clock(clock), .Enable(Enable), .out(out[3:0]), .in(in[3:0]));
endmodule

module C31 (
  input  I7,
  input  I6,
  input  I5,
  input  I4,
  output nI7,
  output I7_2,
  output nI6,
  output I6_2,
  output nI5,
  output I5_2,
  output nI4,
  output I4_2
);

  not not_1 (nI7, I7);
  not not_2 (nI6, I6);
  not not_3 (nI5, I5);
  not not_4 (nI4, I4);

  assign I4_2 = I4;
  assign I5_2 = I5;
  assign I6_2 = I6;
  assign I7_2 = I7;
endmodule

module _4_AND (
  input  _1,
  input  _2,
  input  _4,
  input  _5,
  input  _9,
  input  _10,
  input  _12,
  input  _13,
  output _3,
  output _6,
  output _8,
  output _11
);

  and and_1 (_3, _1, _2);
  and and_2 (_6, _4, _5);
  and and_3 (_8, _9, _10);
  and and_4 (_11, _12, _13);
endmodule

module C48 (
  input  _13,
  input  _12,
  input  _10,
  input  _9,
  input  _6,
  input  _5,
  input  _2,
  input  _1,
  output _11,
  output _8
);

  or or_1 (_11, _13, _12);
  or or_2 (_8, _10, _9, _6, _5, _2, _1);
endmodule

module Register_1bit (
  input  Xi,
  input  Load,
  input  Clk,
  input  Clr,
  input  Enable,
  output Yi
);

  wire and_1_out, and_2_out, d_ff_1_q, not_1_out, or_1_out;

  not not_1 (not_1_out, Load);
  and and_1 (and_1_out, Load, Xi);
  and and_2 (and_2_out, not_1_out, d_ff_1_q);
  or or_1 (or_1_out, and_1_out, and_2_out);
  D_Flip_Flop d_ff_1 (.clk(Clk), .D(or_1_out), .Q(d_ff_1_q), .reset(Clr));  // open: Qn, preset, en
  assign Yi = Enable ? d_ff_1_q : 1'bz;  // Controlled_Buffer controlled_buffer_1
endmodule

module Register_8bit (
  input  [3:0] LSBIN,
  input  [3:0] MSBIN,
  input  Load,
  input  Clk,
  input  Clr,
  output [3:0] MSBOUT,
  output [3:0] LSBOUT
);

  registerUnit R7 (.Xi(MSBIN[3]), .Load(Load), .Clk(Clk), .Clr(Clr), .Enable(1'b1), .Yi(MSBOUT[3]));
  registerUnit R6 (.Xi(MSBIN[2]), .Load(Load), .Clk(Clk), .Clr(Clr), .Enable(1'b1), .Yi(MSBOUT[2]));
  registerUnit R5 (.Xi(MSBIN[1]), .Load(Load), .Clk(Clk), .Clr(Clr), .Enable(1'b1), .Yi(MSBOUT[1]));
  registerUnit R4 (.Xi(MSBIN[0]), .Load(Load), .Clk(Clk), .Clr(Clr), .Enable(1'b1), .Yi(MSBOUT[0]));
  registerUnit R3 (.Xi(LSBIN[3]), .Load(Load), .Clk(Clk), .Clr(Clr), .Enable(1'b1), .Yi(LSBOUT[3]));
  registerUnit R2 (.Xi(LSBIN[2]), .Load(Load), .Clk(Clk), .Clr(Clr), .Enable(1'b1), .Yi(LSBOUT[2]));
  registerUnit R1 (.Xi(LSBIN[1]), .Load(Load), .Clk(Clk), .Clr(Clr), .Enable(1'b1), .Yi(LSBOUT[1]));
  registerUnit R0 (.Xi(LSBIN[0]), .Load(Load), .Clk(Clk), .Clr(Clr), .Enable(1'b1), .Yi(LSBOUT[0]));
endmodule

module sap1 (
  input  CLR,
  output [3:0] High,
  output [3:0] Low,
  output out_4,
  output out_5,
  output out_6,
  output out_7,
  output out_8,
  output out_9,
  output out_10,
  output out_11
);

  wire clock_1_out, controlled_buffer_1_out, controlled_buffer_7_out, controlmatrix_1_cp, controlmatrix_1_ea,
       controlmatrix_1_ep, controlmatrix_1_eu, controlmatrix_1_nce, controlmatrix_1_nei,
       controlmatrix_1_nhlt, controlmatrix_1_nl0, controlmatrix_1_nla, controlmatrix_1_nlb,
       controlmatrix_1_nli, controlmatrix_1_nlm, controlmatrix_1_su, not_1_out, not_2_out, not_3_out,
       not_4_out, not_5_out, not_6_out, not_7_out, not_8_out, not_9_out;
  wire [3:0] Counter_q, IR_lsbout, IR_msbout, MAR_lsbout, RegisterA_lsbout, RegisterA_msbout;
  wire [7:0] adder_1_out, controlled_inverter_1_out, RegisterB_lsbout;

  Counter #(.width(4), .max('hf), .trigger("falling")) Counter (
    .Q(Counter_q), .clk(controlled_buffer_1_out), .clr(CLR));  // open: load, D, count, carry
  assign controlled_buffer_1_out = controlmatrix_1_cp ? controlled_buffer_7_out : 1'bz;  // Controlled_Buffer controlled_buffer_1
  not not_1 (not_1_out, controlmatrix_1_nlm);
  not not_2 (not_2_out, controlmatrix_1_nce);
  register IR (
    .LSBIN(Low), .MSBIN(High), .Load(not_3_out), .Clk(controlled_buffer_7_out), .Clr(CLR),
    .MSBOUT(IR_msbout), .LSBOUT(IR_lsbout));
  not not_3 (not_3_out, controlmatrix_1_nli);
  assign Low = controlmatrix_1_ep ? Counter_q : 4'bz;  // Controlled_Buffer controlled_buffer_2
  register MAR (
    .LSBIN(Low), .Load(not_1_out), .Clk(controlled_buffer_7_out), .Clr(CLR), .LSBOUT(MAR_lsbout));  // open: MSBIN, MSBOUT
  RAM #(.addrWidth(4)) ram_1 (.addr(MAR_lsbout), .data({High, Low}), .ld(not_2_out));  // open: sel, clk, clr
  assign Low = not_4_out ? IR_lsbout : 4'bz;  // Controlled_Buffer controlled_buffer_3
  not not_4 (not_4_out, controlmatrix_1_nei);
  ControlMatrix controlmatrix_1 (
    .nHLT(controlmatrix_1_nhlt), .I7(IR_msbout[3]), .I6(IR_msbout[2]), .I5(IR_msbout[1]), .I4(IR_msbout[0]),
    .CLR(CLR), .nCLK(controlled_buffer_7_out), .Cp(controlmatrix_1_cp), .Ep(controlmatrix_1_ep),
    .nLm(controlmatrix_1_nlm), .nCE(controlmatrix_1_nce), .nLi(controlmatrix_1_nli),
    .nEi(controlmatrix_1_nei), .nLA(controlmatrix_1_nla), .nL0(controlmatrix_1_nl0), .Su(controlmatrix_1_su),
    .Eu(controlmatrix_1_eu), .EA(controlmatrix_1_ea), .nLB(controlmatrix_1_nlb));  // open: Ex, ED, Ec
  assign {High, Low} = controlmatrix_1_ea ? {RegisterA_msbout, RegisterA_lsbout} : 8'bz;  // Controlled_Buffer controlled_buffer_4
  assign {High, Low} = controlmatrix_1_eu ? adder_1_out : 8'bz;  // Controlled_Buffer controlled_buffer_5
  register RegisterA (
    .LSBIN(Low), .MSBIN(High), .Load(not_5_out), .Clk(controlled_buffer_7_out), .Clr(CLR),
    .MSBOUT(RegisterA_msbout), .LSBOUT(RegisterA_lsbout));
  Adder adder_1 (
    .a({RegisterA_msbout, RegisterA_lsbout}), .b(controlled_inverter_1_out), .out(adder_1_out),
    .cin(controlmatrix_1_su));  // open: cout
  not not_5 (not_5_out, controlmatrix_1_nla);
  assign controlled_inverter_1_out = controlmatrix_1_su ? ~RegisterB_lsbout : 8'bz;  // Controlled_Inverter controlled_inverter_1
  not not_6 (not_6_out, controlmatrix_1_nlb);
  register \output  (
    .LSBIN(Low), .MSBIN(High), .Load(not_7_out), .Clk(controlled_buffer_7_out), .Clr(CLR),
    .MSBOUT({out_11, out_10, out_9, out_8}), .LSBOUT({out_7, out_6, out_5, out_4}));
  not not_7 (not_7_out, controlmatrix_1_nl0);
  assign controlled_inverter_1_out = not_8_out ? RegisterB_lsbout : 8'bz;  // Controlled_Buffer controlled_buffer_6
  not not_8 (not_8_out, controlmatrix_1_su);
  Clock clock_1 (.out(clock_1_out));
  not not_9 (not_9_out, controlmatrix_1_nhlt);
  assign controlled_buffer_7_out = not_9_out ? clock_1_out : 1'bz;  // Controlled_Buffer controlled_buffer_7
  register RegisterB (
    .LSBIN(Low), .MSBIN(High), .Load(not_6_out), .Clk(controlled_buffer_7_out), .Clr(CLR),
    .MSBOUT(RegisterB_lsbout[7:4]), .LSBOUT(RegisterB_lsbout[3:0]));
  Hex_Digit_Display hex_digit_display_1 (.value({out_11, out_10, out_9, out_8}));  // open: dp
  Hex_Digit_Display hex_digit_display_2 (.value({out_7, out_6, out_5, out_4}));  // open: dp

  // Notes on the sheet:
  //   ADD/SUB
endmodule

module sap2 (
  input  CLR,
  output [3:0] High,
  output [3:0] Low,
  output out_4,
  output out_5,
  output out_6,
  output out_7,
  output out_8,
  output out_9,
  output out_10,
  output out_11
);

  wire clock_1_out, controlled_buffer_1_out, controlled_buffer_8_out, controlmatrix_1_cp, controlmatrix_1_ea,
       controlmatrix_1_ec, controlmatrix_1_ed, controlmatrix_1_ep, controlmatrix_1_eu, controlmatrix_1_ex,
       controlmatrix_1_nce, controlmatrix_1_nei, controlmatrix_1_nhlt, controlmatrix_1_nl0,
       controlmatrix_1_nla, controlmatrix_1_nlb, controlmatrix_1_nli, controlmatrix_1_nlm,
       controlmatrix_1_su, not_1_out, not_2_out, not_3_out, not_4_out, not_5_out, not_6_out, not_7_out,
       not_8_out, not_9_out;
  wire [3:0] Counter_q, IR_lsbout, IR_msbout, MAR_lsbout, RegisterB_lsbout;
  wire [7:0] adder_1_out, controlled_buffer_7_out, multiplier_1_out, RegisterA_lsbout;
  wire [7:4] RegisterB_msbout;

  Counter #(.width(4), .max('hf), .trigger("falling")) Counter (
    .Q(Counter_q), .clk(controlled_buffer_1_out), .clr(CLR));  // open: load, D, count, carry
  assign controlled_buffer_1_out = controlmatrix_1_cp ? controlled_buffer_8_out : 1'bz;  // Controlled_Buffer controlled_buffer_1
  not not_1 (not_1_out, controlmatrix_1_nlm);
  not not_2 (not_2_out, controlmatrix_1_nce);
  register IR (
    .LSBIN(Low), .MSBIN(High), .Load(not_3_out), .Clk(controlled_buffer_8_out), .Clr(CLR),
    .MSBOUT(IR_msbout), .LSBOUT(IR_lsbout));
  not not_3 (not_3_out, controlmatrix_1_nli);
  assign Low = controlmatrix_1_ep ? Counter_q : 4'bz;  // Controlled_Buffer controlled_buffer_2
  register MAR (
    .LSBIN(Low), .Load(not_1_out), .Clk(controlled_buffer_8_out), .Clr(CLR), .LSBOUT(MAR_lsbout));  // open: MSBIN, MSBOUT
  RAM #(.addrWidth(4)) ram_1 (.addr(MAR_lsbout), .data({High, Low}), .ld(not_2_out));  // open: sel, clk, clr
  not not_4 (not_4_out, controlmatrix_1_nei);
  assign Low = not_4_out ? IR_lsbout : 4'bz;  // Controlled_Buffer controlled_buffer_3
  ControlMatrix controlmatrix_1 (
    .nHLT(controlmatrix_1_nhlt), .I7(IR_msbout[3]), .I6(IR_msbout[2]), .I5(IR_msbout[1]), .I4(IR_msbout[0]),
    .CLR(CLR), .nCLK(controlled_buffer_8_out), .Cp(controlmatrix_1_cp), .Ep(controlmatrix_1_ep),
    .nLm(controlmatrix_1_nlm), .nCE(controlmatrix_1_nce), .nLi(controlmatrix_1_nli),
    .nEi(controlmatrix_1_nei), .nLA(controlmatrix_1_nla), .nL0(controlmatrix_1_nl0), .Su(controlmatrix_1_su),
    .Eu(controlmatrix_1_eu), .EA(controlmatrix_1_ea), .nLB(controlmatrix_1_nlb), .Ex(controlmatrix_1_ex),
    .ED(controlmatrix_1_ed), .Ec(controlmatrix_1_ec));
  assign {High, Low} = controlmatrix_1_ex ? multiplier_1_out : 8'bz;  // Controlled_Buffer controlled_buffer_4
  assign {High, Low} = controlmatrix_1_ea ? RegisterA_lsbout : 8'bz;  // Controlled_Buffer controlled_buffer_5
  assign {High, Low} = controlmatrix_1_eu ? adder_1_out : 8'bz;  // Controlled_Buffer controlled_buffer_6
  not not_5 (not_5_out, controlmatrix_1_nla);
  register RegisterA (
    .LSBIN(Low), .MSBIN(High), .Load(not_5_out), .Clk(controlled_buffer_8_out), .Clr(CLR),
    .MSBOUT(RegisterA_lsbout[7:4]), .LSBOUT(RegisterA_lsbout[3:0]));
  Adder adder_1 (
    .a(RegisterA_lsbout), .b(controlled_buffer_7_out), .out(adder_1_out), .cin(controlmatrix_1_su));  // open: cout
  assign controlled_buffer_7_out = not_8_out ? {RegisterB_msbout, RegisterB_lsbout} : 8'bz;  // Controlled_Buffer controlled_buffer_7
  assign controlled_buffer_7_out = controlmatrix_1_su ? ~{RegisterB_msbout, RegisterB_lsbout} : 8'bz;  // Controlled_Inverter controlled_inverter_1
  not not_6 (not_6_out, controlmatrix_1_nlb);
  register \output  (
    .LSBIN(Low), .MSBIN(High), .Load(not_7_out), .Clk(controlled_buffer_8_out), .Clr(CLR),
    .MSBOUT({out_11, out_10, out_9, out_8}), .LSBOUT({out_7, out_6, out_5, out_4}));
  not not_7 (not_7_out, controlmatrix_1_nl0);
  not not_8 (not_8_out, controlmatrix_1_su);
  Clock clock_1 (.out(clock_1_out));
  not not_9 (not_9_out, controlmatrix_1_nhlt);
  assign controlled_buffer_8_out = not_9_out ? clock_1_out : 1'bz;  // Controlled_Buffer controlled_buffer_8
  register RegisterB (
    .LSBIN(Low), .MSBIN(High), .Load(not_6_out), .Clk(controlled_buffer_8_out), .Clr(CLR),
    .MSBOUT(RegisterB_msbout), .LSBOUT(RegisterB_lsbout));
  Multiplier multiplier_1 (
    .a(RegisterA_lsbout), .b({RegisterB_msbout, RegisterB_lsbout}), .out(multiplier_1_out));  // open: cin, cout
  Hex_Digit_Display hex_digit_display_1 (.value({out_7, out_6, out_5, out_4}));  // open: dp
  Hex_Digit_Display hex_digit_display_2 (.value({out_11, out_10, out_9, out_8}));  // open: dp

  // Notes on the sheet:
  //   ADD/SUB
  //   Multipy
endmodule

module test (
  input  less,
  input  equal,
  input  greater,
  output less_2,
  output equal_2,
  output greater_2
);

  wire c31_1_i4_2, c31_1_i5_2, c31_1_i6_2, c31_1_ni4, c31_1_ni5, c31_1_ni6;

  C31 c31_1 (
    .I7(1'b1), .I6(less), .I5(equal), .I4(greater), .nI6(c31_1_ni6), .I6_2(c31_1_i6_2), .nI5(c31_1_ni5),
    .I5_2(c31_1_i5_2), .nI4(c31_1_ni4), .I4_2(c31_1_i4_2));  // open: nI7, I7_2
  and and_1 (less_2, c31_1_i4_2, c31_1_ni5, c31_1_ni6);
  and and_2 (equal_2, c31_1_i5_2, c31_1_ni4, c31_1_ni6);
  and and_3 (greater_2, c31_1_ni4, c31_1_ni5, c31_1_i6_2);
endmodule

module sap3 (
  input  CLR,
  output [3:0] High,
  output [3:0] Low,
  output out_4,
  output out_5,
  output out_6,
  output out_7,
  output out_8,
  output out_9,
  output out_10,
  output out_11
);

  wire clock_1_out, controlled_buffer_1_out, controlled_buffer_9_out, controlmatrix_1_cp, controlmatrix_1_ea,
       controlmatrix_1_ec, controlmatrix_1_ed, controlmatrix_1_ep, controlmatrix_1_eu, controlmatrix_1_ex,
       controlmatrix_1_nce, controlmatrix_1_nei, controlmatrix_1_nhlt, controlmatrix_1_nl0,
       controlmatrix_1_nla, controlmatrix_1_nlb, controlmatrix_1_nli, controlmatrix_1_nlm,
       controlmatrix_1_su, not_1_out, not_2_out, not_3_out, not_4_out, not_5_out, not_6_out, not_7_out,
       not_8_out, not_9_out;
  wire [3:0] Counter_q, IR_lsbout, IR_msbout, MAR_lsbout;
  wire [7:0] adder_1_out, controlled_buffer_8_out, divider_1_out, multiplier_1_out, RegisterA_lsbout,
       RegisterB_lsbout;

  Counter #(.width(4), .max('hf), .trigger("falling")) Counter (
    .Q(Counter_q), .clk(controlled_buffer_1_out), .clr(CLR));  // open: load, D, count, carry
  assign controlled_buffer_1_out = controlmatrix_1_cp ? controlled_buffer_9_out : 1'bz;  // Controlled_Buffer controlled_buffer_1
  not not_1 (not_1_out, controlmatrix_1_nlm);
  not not_2 (not_2_out, controlmatrix_1_nce);
  register IR (
    .LSBIN(Low), .MSBIN(High), .Load(not_3_out), .Clk(controlled_buffer_9_out), .Clr(CLR),
    .MSBOUT(IR_msbout), .LSBOUT(IR_lsbout));
  not not_3 (not_3_out, controlmatrix_1_nli);
  assign Low = controlmatrix_1_ep ? Counter_q : 4'bz;  // Controlled_Buffer controlled_buffer_2
  register MAR (
    .LSBIN(Low), .Load(not_1_out), .Clk(controlled_buffer_9_out), .Clr(CLR), .LSBOUT(MAR_lsbout));  // open: MSBIN, MSBOUT
  RAM #(.addrWidth(4)) ram_1 (.addr(MAR_lsbout), .data({High, Low}), .ld(not_2_out));  // open: sel, clk, clr
  not not_4 (not_4_out, controlmatrix_1_nei);
  assign Low = not_4_out ? IR_lsbout : 4'bz;  // Controlled_Buffer controlled_buffer_3
  ControlMatrix controlmatrix_1 (
    .nHLT(controlmatrix_1_nhlt), .I7(IR_msbout[3]), .I6(IR_msbout[2]), .I5(IR_msbout[1]), .I4(IR_msbout[0]),
    .CLR(CLR), .nCLK(controlled_buffer_9_out), .Cp(controlmatrix_1_cp), .Ep(controlmatrix_1_ep),
    .nLm(controlmatrix_1_nlm), .nCE(controlmatrix_1_nce), .nLi(controlmatrix_1_nli),
    .nEi(controlmatrix_1_nei), .nLA(controlmatrix_1_nla), .nL0(controlmatrix_1_nl0), .Su(controlmatrix_1_su),
    .Eu(controlmatrix_1_eu), .EA(controlmatrix_1_ea), .nLB(controlmatrix_1_nlb), .Ex(controlmatrix_1_ex),
    .ED(controlmatrix_1_ed), .Ec(controlmatrix_1_ec));
  assign {High, Low} = controlmatrix_1_ed ? divider_1_out : 8'bz;  // Controlled_Buffer controlled_buffer_4
  assign {High, Low} = controlmatrix_1_ex ? multiplier_1_out : 8'bz;  // Controlled_Buffer controlled_buffer_5
  assign {High, Low} = controlmatrix_1_ea ? RegisterA_lsbout : 8'bz;  // Controlled_Buffer controlled_buffer_6
  assign {High, Low} = controlmatrix_1_eu ? adder_1_out : 8'bz;  // Controlled_Buffer controlled_buffer_7
  not not_5 (not_5_out, controlmatrix_1_nla);
  register RegisterA (
    .LSBIN(Low), .MSBIN(High), .Load(not_5_out), .Clk(controlled_buffer_9_out), .Clr(CLR),
    .MSBOUT(RegisterA_lsbout[7:4]), .LSBOUT(RegisterA_lsbout[3:0]));
  Adder adder_1 (
    .a(RegisterA_lsbout), .b(controlled_buffer_8_out), .out(adder_1_out), .cin(controlmatrix_1_su));  // open: cout
  assign controlled_buffer_8_out = not_8_out ? RegisterB_lsbout : 8'bz;  // Controlled_Buffer controlled_buffer_8
  assign controlled_buffer_8_out = controlmatrix_1_su ? ~RegisterB_lsbout : 8'bz;  // Controlled_Inverter controlled_inverter_1
  not not_6 (not_6_out, controlmatrix_1_nlb);
  register \output  (
    .LSBIN(Low), .MSBIN(High), .Load(not_7_out), .Clk(controlled_buffer_9_out), .Clr(CLR),
    .MSBOUT({out_11, out_10, out_9, out_8}), .LSBOUT({out_7, out_6, out_5, out_4}));
  not not_7 (not_7_out, controlmatrix_1_nl0);
  not not_8 (not_8_out, controlmatrix_1_su);
  Clock clock_1 (.out(clock_1_out));
  not not_9 (not_9_out, controlmatrix_1_nhlt);
  assign controlled_buffer_9_out = not_9_out ? clock_1_out : 1'bz;  // Controlled_Buffer controlled_buffer_9
  register RegisterB (
    .LSBIN(Low), .MSBIN(High), .Load(not_6_out), .Clk(controlled_buffer_9_out), .Clr(CLR),
    .MSBOUT(RegisterB_lsbout[7:4]), .LSBOUT(RegisterB_lsbout[3:0]));
  Multiplier multiplier_1 (.a(RegisterA_lsbout), .b(RegisterB_lsbout), .out(multiplier_1_out));  // open: cin, cout
  Divider divider_1 (.a(RegisterA_lsbout), .b(RegisterB_lsbout), .out(divider_1_out));  // open: upper, rem
  Hex_Digit_Display hex_digit_display_1 (.value({out_7, out_6, out_5, out_4}));  // open: dp
  Hex_Digit_Display hex_digit_display_2 (.value({out_11, out_10, out_9, out_8}));  // open: dp

  // Notes on the sheet:
  //   ADD/SUB
  //   Multipy
endmodule
